# Fritzing sketch 4th_Butterworth_VCVS_LPF (saved by Fritzing 0.9.3b)
breadboards: 1

parts:
  IC1 = Dual Op-Amp [package=dip08]
  R1 = Resistor [tolerance=±5% resistance=3.3k package=THT]
  C1 = Film/Foil Capacitor [capacitance=100nF voltage=35V package="5mm [THT, pp]"]
  C2 = Film/Foil Capacitor [capacitance=100nF voltage=35V package="5mm [THT, pp]"]
  R2 = Resistor [tolerance=±5% resistance=12k package=THT]
  R3 = Resistor [tolerance=±5% resistance=15k package=THT]
  R4 = Resistor [tolerance=±5% resistance=33k package=THT]
  C3 = Film/Foil Capacitor [capacitance=100nF voltage=35V package="5mm [THT, pp]"]
  C4 = Film/Foil Capacitor [capacitance=100nF voltage=35V package="5mm [THT, pp]"]
  C5 = Ceramic Capacitor [capacitance=100nF package="100 mil [THT, multilayer]"]
  C6 = Electrolytic Capacitor [capacitance=1µF package="100 mil [THT, electrolytic]"]

nets:
  N1: IC1.A_OUT, IC1.A_-IN, R2.Pin_1, C3.+
  N2: IC1.A_+IN, R3.Pin_0, C4.-
  N3: IC1.A_V-, C1.+, C4.+, C5.1, C6.-
  N4: IC1.B_+IN, R1.Pin_0, C1.-
  N5: IC1.B_-IN, IC1.B_OUT, C2.-
  N6: IC1.A_V+, C5.0, C6.+
  N7: R1.Pin_1, C2.+, R2.Pin_0
  N8: R3.Pin_1, R4.Pin_0, C3.-

notes:
  GND
  +5V
  GND
  NC
  IN
  OUT
