# Fritzing sketch ArduinoLFOwithUI_Output (saved by Fritzing 0.9.3b)
breadboards: 2

parts:
  U1 = mystery part, 14 pins [chip_label=MCP4922]
  C1 = Ceramic Capacitor [capacitance=100nF package="100 mil [THT, multilayer]"]
  パーツ1 = Arduino Uno (Rev3)
  LED1 = LED - 3mm [color="Green (570nm)" package="3 mm [THT]"]
  LED2 = LED - 3mm [color="Green (570nm)" package="3 mm [THT]"]
  LED3 = LED - 3mm [color="Green (570nm)" package="3 mm [THT]"]
  LED4 = LED - 3mm [color="Green (570nm)" package="3 mm [THT]"]
  LED5 = LED - 3mm [color="Green (570nm)" package="3 mm [THT]"]
  R1 = Resistor [tolerance=±5% resistance=1k package=THT]
  R2 = Resistor [tolerance=±5% resistance=1k package=THT]
  R3 = Resistor [tolerance=±5% resistance=1k package=THT]
  R4 = Resistor [tolerance=±5% resistance=1k package=THT]
  R5 = Resistor [tolerance=±5% resistance=1k package=THT]
  S1 = Pushbutton [package="[THT]"]
  R6 = Rotary Potentiometer (Small) [maximum_resistance=100kΩ package=THT]
  R7 = Rotary Potentiometer (Small) [maximum_resistance=100kΩ package=THT]
  R8 = Resistor [tolerance=±5% resistance=150 package=THT]
  C2 = Film/Foil Capacitor [capacitance=100nF voltage=35V package="5mm [THT, pp]"]
  R9 = Resistor [tolerance=±5% resistance=150 package=THT]
  C3 = Film/Foil Capacitor [capacitance=100nF voltage=35V package="5mm [THT, pp]"]
  IC1 = Dual Op-Amp [package=dip08]
  R10 = Rotary Potentiometer (Small) [maximum_resistance=100kΩ package=THT]
  IC2 = Dual Op-Amp [package=dip08]
  IC3 = Dual Op-Amp [package=dip08]
  C4 = Electrolytic Capacitor [capacitance=1µF package="100 mil [THT, electrolytic]"]
  R11 = Resistor [tolerance=±5% resistance=100k package=THT]
  D1 = Rectifier Diode [part_number=1N4001 package="300 mil [THT]"]
  R12 = Resistor [tolerance=±5% resistance=47 package=THT]
  R13 = Rotary Potentiometer (Small) [maximum_resistance=100kΩ package=THT]
  C5 = Ceramic Capacitor [capacitance=100nF package="100 mil [THT, multilayer]"]
  C6 = Ceramic Capacitor [capacitance=100nF package="100 mil [THT, multilayer]"]
  C7 = Ceramic Capacitor [capacitance=100nF package="100 mil [THT, multilayer]"]

nets:
  N1: U1.pin1, U1.pin9, C1.1, パーツ1.5V, R6.leg2, R7.leg2, IC1.A_V+, IC2.A_V+, IC3.A_V+, C5.1, C6.1, C7.1
  N2: U1.pin3, パーツ1.D10_PWM/SS
  N3: U1.pin4, パーツ1.D13/SCK
  N4: U1.pin5, パーツ1.D11_PWM/MOSI
  N5: U1.pin8, パーツ1.D9_PWM
  N6: U1.pin11, U1.pin13, パーツ1.3V3
  N7: U1.pin12, C1.0, パーツ1.GND, パーツ1.D2, R1.Pin_0, R2.Pin_0, R3.Pin_0, R4.Pin_0, R5.Pin_0, S1.Pin_3, S1.Pin_4, R6.leg1, R7.leg1, IC1.B_+IN, R10.leg1, IC2.B_+IN, IC3.B_+IN, R13.leg1, C5.0, C6.0, C7.0
  N8: U1.pin14, R8.Pin_0
  N9: パーツ1.A0, R6.wiper
  N10: パーツ1.A1, R7.wiper
  N11: パーツ1.D3_PWM, LED5.anode
  N12: パーツ1.D4, LED4.anode
  N13: パーツ1.D5_PWM, LED3.anode
  N14: パーツ1.D6_PWM, LED2.anode
  N15: パーツ1.D7, LED1.anode
  N16: LED1.cathode, R1.Pin_1
  N17: LED2.cathode, R2.Pin_1
  N18: LED3.cathode, R3.Pin_1
  N19: LED4.cathode, R4.Pin_1
  N20: LED5.cathode, R5.Pin_1
  N21: S1.Pin_1, S1.Pin_2
  N22: R8.Pin_1, C2.-, R9.Pin_0
  N23: C2.+, C3.+, IC1.A_V-, IC2.A_V-, IC3.A_V-
  N24: R9.Pin_1, C3.-, IC1.A_+IN
  N25: IC1.A_OUT, IC1.A_-IN, R10.leg2
  N26: IC1.B_-IN, IC1.B_OUT
  N27: R10.wiper, C4.+
  N28: IC2.A_OUT, IC2.A_-IN, R12.Pin_1
  N29: IC2.A_+IN, C4.-, R11.Pin_0, D1.anode
  N30: IC2.B_-IN, IC2.B_OUT
  N31: IC3.A_OUT, IC3.A_-IN, R11.Pin_1
  N32: IC3.B_-IN, IC3.B_OUT
  N33: D1.cathode, R13.leg2

notes:
  MCP4922
  1 VDD 14 OUTA
  2 NC 13 VREFA
  3 !CS 12 AVSS
  4 SCK 11 VREFB
  5 SDI 10 OUTB
  6 NC 9 !SHDN
  7 NC 8 LDAC
  GND
  +3.3V
  GND
  +5V
  Rate
  PW
  Wave
  Shape
  OUT
  Level
  Bias
