# Fritzing sketch ArduinoLFOwithUI_Output_r (saved by Fritzing 0.9.3b)
breadboards: 2

parts:
  U1 = mystery part, 14 pins [chip_label=MCP4922]
  C1 = Ceramic Capacitor [capacitance=100nF package="100 mil [THT, multilayer]"]
  パーツ1 = Arduino Uno (Rev3)
  LED1 = LED - 3mm [color="Green (570nm)" package="3 mm [THT]"]
  LED2 = LED - 3mm [color="Green (570nm)" package="3 mm [THT]"]
  LED3 = LED - 3mm [color="Green (570nm)" package="3 mm [THT]"]
  LED4 = LED - 3mm [color="Green (570nm)" package="3 mm [THT]"]
  LED5 = LED - 3mm [color="Green (570nm)" package="3 mm [THT]"]
  R1 = Resistor [tolerance=±5% resistance=1k package=THT]
  R2 = Resistor [tolerance=±5% resistance=1k package=THT]
  R3 = Resistor [tolerance=±5% resistance=1k package=THT]
  R4 = Resistor [tolerance=±5% resistance=1k package=THT]
  R5 = Resistor [tolerance=±5% resistance=1k package=THT]
  S1 = Pushbutton [package="[THT]"]
  R6 = Rotary Potentiometer (Small) [maximum_resistance=100kΩ package=THT]
  R7 = Rotary Potentiometer (Small) [maximum_resistance=100kΩ package=THT]
  R8 = Resistor [tolerance=±5% resistance=200 package=THT]
  C2 = Film/Foil Capacitor [capacitance=100nF voltage=35V package="5mm [THT, pp]"]
  R9 = Resistor [tolerance=±5% resistance=200 package=THT]
  C3 = Film/Foil Capacitor [capacitance=100nF voltage=35V package="5mm [THT, pp]"]
  R10 = Rotary Potentiometer (Small) [maximum_resistance=100kΩ package=THT]
  IC2 = Dual Op-Amp [package=dip08]
  C4 = Electrolytic Capacitor [capacitance=1µF package="100 mil [THT, electrolytic]"]
  R11 = Resistor [tolerance=±5% resistance=330k package=THT]
  D1 = Rectifier Diode [part_number=1N4001 package="300 mil [THT]"]
  R12 = Resistor [tolerance=±5% resistance=47 package=THT]
  R13 = Rotary Potentiometer (Small) [maximum_resistance=100kΩ package=THT]
  C5 = Ceramic Capacitor [capacitance=100nF package="100 mil [THT, multilayer]"]
  C6 = Electrolytic Capacitor [capacitance=1µF package="100 mil [THT, electrolytic]"]
  R14 = Resistor [tolerance=±5% resistance=200 package=THT]
  R15 = Resistor [tolerance=±5% resistance=200 package=THT]
  C7 = Film/Foil Capacitor [capacitance=100nF voltage=35V package="5mm [THT, pp]"]
  C8 = Film/Foil Capacitor [capacitance=100nF voltage=35V package="5mm [THT, pp]"]
  R16 = Resistor [tolerance=±5% resistance=10k package=THT]
  D2 = Rectifier Diode [part_number=1N4001 package="300 mil [THT]"]

nets:
  N1: U1.pin1, U1.pin9, C1.1, パーツ1.5V, R6.leg2, R7.leg2, IC2.A_V+, C5.1, C6.+
  N2: U1.pin3, パーツ1.D10_PWM/SS
  N3: U1.pin4, パーツ1.D13/SCK
  N4: U1.pin5, パーツ1.D11_PWM/MOSI
  N5: U1.pin8, パーツ1.D9_PWM
  N6: U1.pin11, U1.pin12, C1.0, パーツ1.GND, パーツ1.D2, R1.Pin_0, R2.Pin_0, R3.Pin_0, R4.Pin_0, R5.Pin_0, S1.Pin_3, S1.Pin_4, R6.leg1, R7.leg1, R10.leg1, R13.leg1, C5.0, C6.-, C7.+, C8.+, R16.Pin_1, D2.anode
  N7: U1.pin13, R10.wiper
  N8: U1.pin14, R8.Pin_0
  N9: パーツ1.A0, R6.wiper
  N10: パーツ1.A1, R7.wiper
  N11: パーツ1.D3_PWM, LED5.anode
  N12: パーツ1.D4, LED4.anode
  N13: パーツ1.D5_PWM, LED3.anode
  N14: パーツ1.D6_PWM, LED2.anode
  N15: パーツ1.D7, LED1.anode
  N16: パーツ1.3V3, R10.leg2, R13.leg2
  N17: LED1.cathode, R1.Pin_1
  N18: LED2.cathode, R2.Pin_1
  N19: LED3.cathode, R3.Pin_1
  N20: LED4.cathode, R4.Pin_1
  N21: LED5.cathode, R5.Pin_1
  N22: S1.Pin_1, S1.Pin_2
  N23: R8.Pin_1, C2.-, R9.Pin_0
  N24: C2.+, C3.+, IC2.A_V-
  N25: R9.Pin_1, C3.-, R14.Pin_0
  N26: IC2.A_OUT, IC2.A_-IN, R12.Pin_1
  N27: IC2.A_+IN, C4.-, R11.Pin_0, D1.anode, D2.cathode
  N28: IC2.B_+IN, R13.wiper
  N29: IC2.B_-IN, IC2.B_OUT, R11.Pin_1
  N30: C4.+, R15.Pin_1, C8.-
  N31: R12.Pin_0, R16.Pin_0
  N32: R14.Pin_1, R15.Pin_0, C7.-

notes:
  MCP4922
  1 VDD 14 OUTA
  2 NC 13 VREFA
  3 !CS 12 AVSS
  4 SCK 11 VREFB
  5 SDI 10 OUTB
  6 NC 9 !SHDN
  7 NC 8 LDAC
  GND
  +3.3V
  GND
  +5V
  Rate
  PW
  Wave
  Shape
  OUT
  Level
  Bias
