# Fritzing sketch OutputBoard_MFB (saved by Fritzing 0.9.3b)
breadboards: 1

parts:
  IC1 = Dual Op-Amp [package=dip08]
  R1 = Resistor [tolerance=±5% resistance=3.3k package=THT]
  C1 = Film/Foil Capacitor [capacitance=100nF voltage=35V package="5mm [THT, pp]"]
  C2 = Film/Foil Capacitor [capacitance=100nF voltage=35V package="5mm [THT, pp]"]
  R2 = Resistor [tolerance=±5% resistance=12k package=THT]
  R3 = Resistor [tolerance=±5% resistance=15k package=THT]
  R4 = Resistor [tolerance=±5% resistance=33k package=THT]
  C3 = Film/Foil Capacitor [capacitance=100nF voltage=35V package="5mm [THT, pp]"]
  C4 = Film/Foil Capacitor [capacitance=100nF voltage=35V package="5mm [THT, pp]"]
  C5 = Ceramic Capacitor [capacitance=100nF package="100 mil [THT, multilayer]"]
  C6 = Electrolytic Capacitor [capacitance=1µF package="100 mil [THT, electrolytic]"]
  IC2 = Dual Op-Amp [package=dip08]
  C7 = Electrolytic Capacitor [capacitance=1µF package="100 mil [THT, electrolytic]"]
  R6 = Resistor [tolerance=±5% resistance=330k package=THT]
  D1 = Rectifier Diode [part_number=1N4001 package="300 mil [THT]"]
  R7 = Resistor [tolerance=±5% resistance=33 package=THT]
  C8 = Ceramic Capacitor [capacitance=100nF package="100 mil [THT, multilayer]"]
  R8 = Rotary Potentiometer (Small) [maximum_resistance=100kΩ package=THT]
  D2 = Rectifier Diode [part_number=1N4001 package="300 mil [THT]"]

nets:
  N1: IC1.A_OUT, IC1.A_-IN, R2.Pin_1, C3.+
  N2: IC1.A_+IN, R3.Pin_0, C4.-
  N3: IC1.A_V-, C1.+, C4.+, C5.1, C6.-, IC2.A_V-, D1.anode, C8.1, R8.leg1
  N4: IC1.B_+IN, R1.Pin_0, C1.-
  N5: IC1.B_-IN, IC1.B_OUT, C2.-, C7.+
  N6: IC1.A_V+, C5.0, C6.+, IC2.A_V+, C8.0
  N7: R1.Pin_1, C2.+, R2.Pin_0
  N8: R3.Pin_1, R4.Pin_0, C3.-
  N9: IC2.A_OUT, IC2.A_-IN, R6.Pin_1
  N10: IC2.A_+IN, R8.wiper
  N11: IC2.B_+IN, C7.-, R6.Pin_0, D1.cathode, D2.anode
  N12: IC2.B_-IN, IC2.B_OUT, R7.Pin_1
  N13: R8.leg2, D2.cathode

notes:
  GND
  +5V
  GND
  +3.3V
  IN
  OUT
