# Fritzing sketch OutputBoard_RC_LPF (saved by Fritzing 0.9.3b)
breadboards: 1

parts:
  C6 = Electrolytic Capacitor [capacitance=1µF package="100 mil [THT, electrolytic]"]
  IC2 = Dual Op-Amp [package=dip08]
  C7 = Electrolytic Capacitor [capacitance=1µF package="100 mil [THT, electrolytic]"]
  R5 = Resistor [tolerance=±5% resistance=100 package=THT]
  R6 = Resistor [tolerance=±5% resistance=330k package=THT]
  D1 = Rectifier Diode [part_number=1N4001 package="300 mil [THT]"]
  R7 = Resistor [tolerance=±5% resistance=33 package=THT]
  C8 = Ceramic Capacitor [capacitance=100nF package="100 mil [THT, multilayer]"]
  R8 = Rotary Potentiometer (Small) [maximum_resistance=100kΩ package=THT]
  C9 = Film/Foil Capacitor [capacitance=100nF voltage=35V package="5mm [THT, pp]"]
  R9 = Resistor [tolerance=±5% resistance=200 package=THT]
  R10 = Resistor [tolerance=±5% resistance=200 package=THT]
  R11 = Resistor [tolerance=±5% resistance=200 package=THT]
  R12 = Resistor [tolerance=±5% resistance=200 package=THT]
  C10 = Film/Foil Capacitor [capacitance=100nF voltage=35V package="5mm [THT, pp]"]
  C11 = Film/Foil Capacitor [capacitance=100nF voltage=35V package="5mm [THT, pp]"]
  C12 = Film/Foil Capacitor [capacitance=100nF voltage=35V package="5mm [THT, pp]"]
  D2 = Rectifier Diode [part_number=1N4001 package="300 mil [THT]"]

nets:
  N1: C6.-, IC2.A_V-, D1.anode, C8.1, R8.leg1, C9.-, C10.-, C11.-, C12.-
  N2: C6.+, IC2.A_V+, C8.0
  N3: IC2.A_OUT, IC2.A_-IN, R6.Pin_1
  N4: IC2.A_+IN, R8.wiper
  N5: IC2.B_+IN, R5.Pin_0, D1.cathode, D2.anode
  N6: IC2.B_-IN, IC2.B_OUT, R7.Pin_1
  N7: C7.-, R5.Pin_1, R6.Pin_0
  N8: C7.+, C9.+, R9.Pin_0
  N9: R8.leg2, D2.cathode
  N10: R9.Pin_1, R10.Pin_0, C10.+
  N11: R10.Pin_1, R11.Pin_0, C11.+
  N12: R11.Pin_1, R12.Pin_0, C12.+

notes:
  GND
  +5V
  GND
  +3.3V
  IN
  OUT
