# Fritzing sketch ArduinoLFO (saved by Fritzing 0.9.3b)
breadboards: 1

parts:
  U1 = mystery part, 14 pins [chip_label=MCP4922]
  C1 = Ceramic Capacitor [capacitance=100nF package="100 mil [THT, multilayer]"]
  パーツ1 = Arduino Uno (Rev3)

nets:
  N1: U1.pin1, U1.pin9, C1.1, パーツ1.5V
  N2: U1.pin3, パーツ1.D10_PWM/SS
  N3: U1.pin4, パーツ1.D13/SCK
  N4: U1.pin5, パーツ1.D11_PWM/MOSI
  N5: U1.pin8, パーツ1.D9_PWM
  N6: U1.pin11, U1.pin13, パーツ1.3V3
  N7: U1.pin12, C1.0, パーツ1.GND

notes:
  MCP4922
  1 VDD 14 OUTA
  2 NC 13 VREFA
  3 !CS 12 AVSS
  4 SCK 11 VREFB
  5 SDI 10 OUTB
  6 NC 9 !SHDN
  7 NC 8 LDAC
  OUTA
  GND
  +3.3V
  GND
  +5V
  OUTB
