# Fritzing sketch ArduinoLFO_MainBoard_Test (saved by Fritzing 0.9.3b)
breadboards: 1

parts:
  パーツ1 = Arduino Nano (Rev3.0) (ICSP)
  R1 = Resistor [tolerance=±5% resistance=1k package=THT]
  LED1 = LED - 3mm [color="Green (570nm)" package="3 mm [THT]"]
  R2 = Resistor [tolerance=±5% resistance=1k package=THT]
  R3 = Resistor [tolerance=±5% resistance=1k package=THT]
  R4 = Resistor [tolerance=±5% resistance=1k package=THT]
  LED2 = LED - 3mm [color="Green (570nm)" package="3 mm [THT]"]
  LED3 = LED - 3mm [color="Green (570nm)" package="3 mm [THT]"]
  LED4 = LED - 3mm [color="Green (570nm)" package="3 mm [THT]"]
  S1 = Pushbutton [package="[THT]"]
  IC1 = IC, DIP package, 14 pins [chip_label=MCP4922]
  VCC1 = Battery block 9V
  C1 = Ceramic Capacitor [capacitance=100nF package="100 mil [THT, multilayer]"]
  R5 = Rotary Potentiometer (Small) [maximum_resistance=100kΩ package=THT]
  R6 = Rotary Potentiometer (Small) [maximum_resistance=100kΩ package=THT]
  R7 = Rotary Potentiometer (Small) [maximum_resistance=100kΩ package=THT]
  C2 = Electrolytic Capacitor [capacitance=0.1mF package="100 mil [THT, electrolytic]"]
  R8 = Resistor [tolerance=±5% resistance=10k package=THT]

nets:
  N1: パーツ1.GND, LED1.cathode, LED2.cathode, LED3.cathode, LED4.cathode, S1.Pin_1, S1.Pin_2, IC1.pin11, IC1.pin12, VCC1.-, C1.0, R5.leg1, R6.leg1, R7.leg2, C2.-, R8.Pin_0
  N2: パーツ1.D2, S1.Pin_4
  N3: パーツ1.D3, R8.Pin_1
  N4: パーツ1.D4, R2.Pin_0, R2.Pin_1
  N5: パーツ1.D5, R3.Pin_0, R3.Pin_1
  N6: パーツ1.D6, R4.Pin_0, R4.Pin_1
  N7: パーツ1.D7, R1.Pin_0, R1.Pin_1
  N8: パーツ1.D9, IC1.pin8
  N9: パーツ1.D10, IC1.pin3
  N10: パーツ1.D11/MOSI, IC1.pin5
  N11: パーツ1.VIN, VCC1.+
  N12: パーツ1.5V, IC1.pin1, IC1.pin9, C1.1, R5.leg2, R6.leg2, C2.+
  N13: パーツ1.A1, R6.wiper
  N14: パーツ1.A0, R5.wiper
  N15: パーツ1.3V3, R7.leg1
  N16: パーツ1.D13/SCK, IC1.pin4
  N17: IC1.pin13, R7.wiper

notes:
  SyncIn
  MCP4922
  1 VDD 14 OUTA
  2 NC 13 VREFA
  3 !CS 12 AVSS
  4 SCK 11 VREFB
  5 SDI 10 OUTB
  6 NC 9 !SHDN
  7 NC 8 LDAC
  OUTA
  GND
  3.3V
  GND
  5V
  Wave Shape
  RATE
  10k/A
  PW
  10k/B
  VREFA
  10k/B
