# Fritzing sketch ArduinoLFOwithUI (saved by Fritzing 0.9.3b)
breadboards: 1

parts:
  U1 = mystery part, 14 pins [chip_label=MCP4922]
  C1 = Ceramic Capacitor [capacitance=100nF package="100 mil [THT, multilayer]"]
  パーツ1 = Arduino Uno (Rev3)
  LED1 = LED - 3mm [color="Green (570nm)" package="3 mm [THT]"]
  LED2 = LED - 3mm [color="Green (570nm)" package="3 mm [THT]"]
  LED3 = LED - 3mm [color="Green (570nm)" package="3 mm [THT]"]
  LED4 = LED - 3mm [color="Green (570nm)" package="3 mm [THT]"]
  LED5 = LED - 3mm [color="Green (570nm)" package="3 mm [THT]"]
  R1 = Resistor [tolerance=±5% resistance=1k package=THT]
  R2 = Resistor [tolerance=±5% resistance=1k package=THT]
  R3 = Resistor [tolerance=±5% resistance=1k package=THT]
  R4 = Resistor [tolerance=±5% resistance=1k package=THT]
  R5 = Resistor [tolerance=±5% resistance=1k package=THT]
  S1 = Pushbutton [package="[THT]"]
  R6 = Rotary Potentiometer (Small) [maximum_resistance=100kΩ package=THT]
  R7 = Rotary Potentiometer (Small) [maximum_resistance=100kΩ package=THT]

nets:
  N1: U1.pin1, U1.pin9, C1.1, パーツ1.5V, R6.leg2, R7.leg2
  N2: U1.pin3, パーツ1.D10_PWM/SS
  N3: U1.pin4, パーツ1.D13/SCK
  N4: U1.pin5, パーツ1.D11_PWM/MOSI
  N5: U1.pin8, パーツ1.D9_PWM
  N6: U1.pin11, U1.pin13, パーツ1.3V3
  N7: U1.pin12, C1.0, パーツ1.GND, パーツ1.D2, R1.Pin_0, R2.Pin_0, R3.Pin_0, R4.Pin_0, R5.Pin_0, S1.Pin_3, S1.Pin_4, R6.leg1, R7.leg1
  N8: パーツ1.A0, R6.wiper
  N9: パーツ1.A1, R7.wiper
  N10: パーツ1.D3_PWM, LED5.anode
  N11: パーツ1.D4, LED4.anode
  N12: パーツ1.D5_PWM, LED3.anode
  N13: パーツ1.D6_PWM, LED2.anode
  N14: パーツ1.D7, LED1.anode
  N15: LED1.cathode, R1.Pin_1
  N16: LED2.cathode, R2.Pin_1
  N17: LED3.cathode, R3.Pin_1
  N18: LED4.cathode, R4.Pin_1
  N19: LED5.cathode, R5.Pin_1
  N20: S1.Pin_1, S1.Pin_2

notes:
  MCP4922
  1 VDD 14 OUTA
  2 NC 13 VREFA
  3 !CS 12 AVSS
  4 SCK 11 VREFB
  5 SDI 10 OUTB
  6 NC 9 !SHDN
  7 NC 8 LDAC
  OUTA
  GND
  +3.3V
  GND
  +5V
  OUTB
  Rate
  PW
  Wave
  Shape
