# Fritzing sketch ArduinoLFOケース内配線 (saved by Fritzing 0.9.3b)
perfboards: 2

parts:
  J1 = female pin header, 2 pins [form="♀ (female)"]
  J2 = female pin header, 3 pins [form="♀ (female)"]
  J3 = female pin header, 3 pins [form="♀ (female)"]
  J4 = female pin header, 3 pins [form="♀ (female)"]
  J5 = female pin header, 3 pins [form="♀ (female)"]
  J6 = female pin header, 2 pins [form="♀ (female)"]
  J7 = female pin header, 2 pins [form="♀ (female)"]
  J8 = female pin header, 2 pins [form="♀ (female)"]
  R1 = Rotary Potentiometer (Small) [maximum_resistance=100kΩ package=THT]
  Power_plug1 = Power plug
  S1 = Round Pushbutton
  TRS1 = Audio Jack (TRS) 3.5mm [package="4Ucon 08780 [THT]"]
  R2 = Rotary Potentiometer (Small) [maximum_resistance=100kΩ package=THT]
  R3 = Rotary Potentiometer (Small) [maximum_resistance=100kΩ package=THT]
  R4 = Rotary Potentiometer (Small) [maximum_resistance=100kΩ package=THT]
  TRS2 = Audio Jack (TRS) 3.5mm [package="4Ucon 08780 [THT]"]
  S2 = Taiway 100-SP-X-T1 SPDT Miniature Toggle Switch [part_number=100-SP-X-T1-0-0-B1-M1 package=THT]
  S3 = Taiway 100-SP-X-T1 SPDT Miniature Toggle Switch [part_number=100-SP-X-T1-0-0-B1-M1 package=THT]
  J9 = female pin header, 3 pins [form="♀ (female)"]
  J10 = female pin header, 3 pins [form="♀ (female)"]
  J11 = female pin header, 2 pins [form="♀ (female)"]
  J12 = female pin header, 2 pins [form="♀ (female)"]  # not connected
  J13 = female pin header, 2 pins [form="♀ (female)"]
  J14 = female pin header, 2 pins [form="♀ (female)"]

nets:
  N1: J1.pin1, Power_plug1.GND
  N2: J1.pin2, S2.L2
  N3: J2.pin1, J9.pin1
  N4: J2.pin2, J9.pin2
  N5: J2.pin3, J9.pin3
  N6: J3.pin1, R3.wiper
  N7: J3.pin2, R3.leg2
  N8: J3.pin3, R3.leg1
  N9: J4.pin1, R2.leg2
  N10: J4.pin2, R2.leg1
  N11: J4.pin3, R2.wiper
  N12: J5.pin1, R1.leg2
  N13: J5.pin2, R1.leg1
  N14: J5.pin3, R1.wiper
  N15: J6.pin1, J11.pin1
  N16: J6.pin2, J11.pin2
  N17: J7.pin1, S1.leg0
  N18: J7.pin2, S1.leg1
  N19: J8.pin1, TRS1.Sleeve
  N20: J8.pin2, TRS1.Tip
  N21: Power_plug1.VCC, S2.L1
  N22: R4.leg1, J10.pin1
  N23: R4.wiper, J10.pin2
  N24: R4.leg2, J10.pin3
  N25: TRS2.Tip, J14.pin2
  N26: S3.L1, J13.pin1
  N27: S3.L2, J13.pin2

notes:
  Rate
  10k/A
  PW
  10k/B
  PWR
  OUT
  PWR
  IN (9V)
  VREF
  10k/B
  OUTA
  Wave
  Shape
  Sync
  In
  Main
  Board
  OutPut
  Board
  BIAS
  10k/B
  Wave
  In
  PWR
  IN
  Wave
  Out
  PWR SW
  Limitter
  GND
